# Fritzing sketch p3 (saved by Fritzing 1.0.1rc)
breadboards: 1

parts:
  Componente3 = Arduino Uno (Rev3) - ICSP
  LCD2 = LCD screen
  LED3 = LED - 3mm [color="Blue (430nm)" current=0.030 package="3 mm [THT]"]
  LED4 = LED - 3mm [color="Yellow (585nm)" current=0.030 package="3 mm [THT]"]
  Componente4 = Thumb Joystick
  S2 = Pushbutton [package="[THT]"]
  HC-SR04_Sensor_2 = HC-SR04 Ultrasonic Distance Sensor
  R5 = Resistor [tolerance=±5% power=0.25 resistance=220 package=THT]
  R6 = Resistor [tolerance=±5% power=0.25 resistance=220 package=THT]
  R7 = Resistor [tolerance=±5% power=0.25 resistance=220 package=THT]
  R8 = Rotary Potentiometer (Large) [maximum_resistance=100kΩ knob_status=50% package=THT]
  DHT1 = DHT11 Humitidy and Temperature Sensor (3 pins)

nets:
  N1: Componente3.A0, Componente4.VERT
  N2: Componente3.A1, Componente4.HORZ
  N3: Componente3.A4/SDA, HC-SR04_Sensor_2.ECHO
  N4: Componente3.ICSP_MISO, Componente3.D12/MISO, LCD2.RS
  N5: Componente3.D8, LCD2.DB5
  N6: Componente3.D9_PWM, LCD2.DB6
  N7: Componente3.D10_PWM/SS, LCD2.DB7
  N8: Componente3.D11_PWM/MOSI, LCD2.E
  N9: Componente3.D2, S2.Pin_3, S2.Pin_4
  N10: Componente3.D3_PWM, Componente4.VCC
  N11: Componente3.D4, DHT1.Plus
  N12: Componente3.D5_PWM, HC-SR04_Sensor_2.TRIG
  N13: Componente3.D6_PWM, R6.Pin_0
  N14: Componente3.D7, LCD2.DB4
  5V: Componente3.5V, LCD2.VDD, Componente4.SEL, HC-SR04_Sensor_2.VCC, R7.Pin_1, DHT1.Signal
  GND: Componente3.GND, LCD2.VSS, LCD2.R/W, LCD2.LED-, LED3.cathode, LED4.cathode, Componente4.GND, S2.Pin_1, S2.Pin_2, HC-SR04_Sensor_2.GND, R8.leg1, R8.leg2, DHT1.Gnd
  N15: LCD2.V0, R8.wiper
  N16: LCD2.LED+, R7.Pin_0
  N17: LED3.anode, R5.Pin_0

custom parts:
  DHT11 Humitidy and Temperature Sensor (3 pins): DHT11 Humidity and Temperature Sensor (3 pins).
